# Fritzing sketch attiny2313 rgb led (saved by Fritzing 0.7.10b)
breadboards: 1

parts:
  S1 = Pushbutton [package="[THT]"]
  S2 = Pushbutton [package="[THT]"]
  R1 = Resistor [resistance=330 tolerance=±5% package=THT]
  R2 = Resistor [resistance=330 tolerance=±5% package=THT]
  R3 = Resistor [resistance=330 tolerance=±5% package=THT]
  LED1 = RGB LED (com. cathode, rbg) [package="5 mm [THT]"]
  U1 = ATtiny2313
  J1 = shrouded pin header, 6 pins [form="♂ (shrouded male)"]
  C1 = Ceramic Capacitor [capacitance=100nF package="100 mil [THT, multilayer]"]

nets:
  N1: S1.Pin_1, S1.Pin_2, U1.Pin_2
  GND: S1.Pin_3, S1.Pin_4, S2.Pin_3, S2.Pin_4, LED1.common_cathode, U1.Pin_10, J1.pin6, C1.1
  N2: S2.Pin_1, S2.Pin_2, U1.Pin_3
  N3: R1.Pin_0, U1.Pin_12
  N4: R1.Pin_1, LED1.green_anode
  N5: R2.Pin_0, U1.Pin_13
  N6: R2.Pin_1, LED1.blue_anode
  N7: R3.Pin_0, U1.Pin_14
  N8: R3.Pin_1, LED1.red_anode
  N9: U1.Pin_1, J1.pin5
  N10: U1.Pin_17, J1.pin4
  N11: U1.Pin_18, J1.pin1
  N12: U1.Pin_19, J1.pin3
  5V: U1.Pin_20, J1.pin2, C1.0

notes:
  ATtiny2313 RGB LED Project
  A small ATtiny2313 project to control an RGB LED connected to pins 0-2 of PORTB.
  Switches on pins 0 and 1 of PORTD control the behavior of the LED.
  Souce code on GitHub at https://github.com/dragongears/AVR-ATtiny2313-RGB-LED-Glow-Ball-Project
  LED1 RGB LED - (4 legs)
  R1 330Ω Resistor
  R2 330Ω Resistor
  R3 330Ω Resistor
  C1 0.1 uF capacitor
  S1 Pushbutton
  S2 Pushbutton
  U1 ATtiny2313
  VCC
  MOSI
  GND
  MISO
  SCK
  RESET
  _____
  PD0
  PD1
  PB0
  PB1
  PB2
  The pin connections on the header in Breadboard view are incorrect and will be fixed when I make the correct part for Fritzing.

custom parts:
  ATtiny2313: Atmel ATtiny2313 microcontroller.
